// Digital circuit Simplic-Refactor.dig as structural Verilog
module Simplic_Refactor (
  input  [15:0] in_1,
  input  in_2,
  input  in_3,
  input  in_4,
  input  in_5,
  input  in_6,
  input  in_7,
  input  in_8,
  input  in_9
);

  wire undriven_5;
  wire [1:0] INSTR_d_2, INSTR_d_3;
  wire [3:0] INSTR_d_4;
  wire [7:0] INSTR_d;
  wire [15:0] bitextender_1_out, div_1_q, div_1_r, div_2_q, div_2_r, mul_1_mul, mul_1_mul_2, mul_2_mul,
       mul_2_mul_2, neg_1_out, not_1_out, undriven, undriven_2, undriven_3, undriven_4, undriven_6,
       undriven_7;

  ROM #(.bigEndian("true"), .AddrBits(16), .Bits(16)) INSTR (
    .A(in_1), .sel(1'b1), .D({INSTR_d_4, INSTR_d_3, INSTR_d_2, INSTR_d}));
  BitExtender bitextender_1 (.in(INSTR_d), .out(bitextender_1_out));
  BarrelShifter #(.Bits(16), .barrelSigned("true")) barrelshifter_1 ();  // open: in, shift, out
  BarrelShifter #(.Bits(16), .barrelSigned("true"), .direction("right")) barrelshifter_2 ();  // open: in, shift, out
  BarrelShifter #(.Bits(16), .barrelShifterMode("arithmetic"), .barrelSigned("true"), .direction("right")) barrelshifter_3 ();  // open: in, shift, out
  BarrelShifter #(.Bits(16), .barrelShifterMode("rotate"), .barrelSigned("true"), .direction("right")) barrelshifter_4 ();  // open: in, shift, out
  Add #(.Bits(16)) add_1 ();  // open: a, b, c_i, s, c_o
  Sub #(.Bits(16)) sub_1 ();  // open: a, b, c_i, s, c_o
  Mul #(.Signed("true"), .Bits(16)) mul_1 (.mul({mul_1_mul_2, mul_1_mul}));  // open: a, b
  Mul #(.Bits(16)) mul_2 (.mul({mul_2_mul_2, mul_2_mul}));  // open: a, b
  Div #(.Signed("true"), .Bits(16)) div_1 (.q(div_1_q), .r(div_1_r));  // open: a, b
  Div #(.Bits(16)) div_2 (.q(div_2_q), .r(div_2_r));  // open: a, b
  Multiplexer #(.Bits(16), .Selector_Bits(2)) multiplexer_1 (
    .in_0(mul_1_mul), .in_1(mul_1_mul_2), .in_2(mul_2_mul), .in_3(mul_2_mul_2));  // open: sel, out
  Multiplexer #(.Selector_Bits(2), .Bits(16)) multiplexer_2 (
    .in_0(div_1_q), .in_1(div_1_r), .in_2(div_2_q), .in_3(div_2_r));  // open: sel, out
  // And and_1 has open pins: In_1=undriven, In_2=undriven_2, out=open
  // Or or_1 has open pins: In_1=undriven_3, In_2=undriven_4, out=open
  assign not_1_out = ~undriven_6;  // Not not_1, 16 bits wide
  Neg #(.Bits(16)) neg_1 (.in(undriven_7), .out(neg_1_out));
  Multiplexer #(.Bits(16)) multiplexer_3 (.sel(undriven_5), .in_0(not_1_out), .in_1(neg_1_out));  // open: out

  // Other names for the same wires on the sheet: PC[15:0] = in_1

  // Notes on the sheet:
  //   contents of INSTR (hex, n*v repeats v):
  //   3183,2321,2000,2000,100
  //   opcode4
  //   control4
  //   s-imm8
  //   u-imm8
  //   flag2
  //   mode2
  //   Z write
  //   Z clear
  //   N write
  //   N clear
  //   C write
  //   C clear
  //   V write
  //   V clear
endmodule
